# Fritzing sketch Schéma Arduino v_1.0 (saved by Fritzing 0.9.3b)
breadboards: 1

parts:
  Composant1 = Arduino Uno (Rev3)
  Composant2 = Arduino Motor Shield (Rev3)
  M1 = DC Motor
  M2 = DC Motor
  VCC1 = Battery block 9V
  Composant3 = Bluetooth HC-05 Macho

nets:
  N1: Composant1.D0/RX, Composant3.TXD
  N2: Composant1.D1/TX, Composant3.RXD
  5V: Composant1.5V, Composant3.VCC
  GND: Composant1.GND, Composant3.GND
  N3: Composant2.B-, M2.pin_2
  N4: Composant2.B+, M2.pin_1
  N5: Composant2.A-, M1.pin_2
  N6: Composant2.A+, M1.pin_1
  N7: Composant2.VMOT, VCC1.+
  N8: Composant2.GND, VCC1.-
